# Fritzing sketch CDS_LCD (saved by Fritzing 0.8.7b)
breadboards: 1

parts:
  부품1 = Arduino Uno (Rev3)
  부품2 = LCD1602-I2C
  Mod2 = KY-015 Temperature & Humidity Sensor Module [package="Breakout board"]
  R1 = Resistor [tolerance=±5% resistance=1k package=THT]
  R2 = Photocell (LDR) [package=THT]

nets:
  N1: 부품1.A0, R1.Pin_0, R2.pin_1
  N2: 부품1.A4/SDA, 부품2.SDA
  N3: 부품1.A5/SCL, 부품2.SCL
  N4: 부품1.D2, Mod2.S
  5V: 부품1.5V, 부품2.VCC, Mod2.Vin, R2.pin_0
  GND: 부품1.GND, 부품2.GND, R1.Pin_1

custom parts:
  LCD1602-I2C: A standard character display, usually with 2x16 characters. Comes in many colors with LCM1602 IIC attached.
  KY-015 Temperature & Humidity Sensor Module: KY-015 temperature and humidity sensor module, provides a low-latency serial interface to measure humidity and temperature.
