# Fritzing sketch LCD (saved by Fritzing 0.8.7b)
breadboards: 1

parts:
  부품1 = Arduino Uno (Rev3)
  부품2 = LCD1602-I2C

nets:
  N1: 부품1.A4/SDA, 부품2.SDA
  N2: 부품1.A5/SCL, 부품2.SCL
  5V: 부품1.5V, 부품2.VCC
  GND: 부품1.GND, 부품2.GND

custom parts:
  LCD1602-I2C: A standard character display, usually with 2x16 characters. Comes in many colors with LCM1602 IIC attached.
