# Fritzing sketch RGB_LED (saved by Fritzing 0.8.7b)
breadboards: 1

parts:
  R1 = Resistor [tolerance=±5% resistance=330 package=THT]
  부품1 = Arduino Uno (Rev3)
  LED1 = RGB LED (com. anode, rbg) [package="5 mm [THT]"]

nets:
  N1: R1.Pin_0, 부품1.GND
  N2: R1.Pin_1, LED1.common_anode
  N3: 부품1.D9_PWM, LED1.red_cathode
  N4: 부품1.D10_PWM/SS, LED1.blue_cathode
  N5: 부품1.D11_PWM/MOSI, LED1.green_cathode
